# Fritzing sketch Katana Sketch (saved by Fritzing 0.9.3b)
breadboards: 3

parts:
  R1 = Resistor [tolerance=±5% resistance=22k package=THT]
  Composant1 = Arduino Nano (Rev3.0) (ICSP)
  S1 = Pushbutton [package="[SMD]"]
  S2 = 0.91 inch OLED I2C Display 128 x 32 Pixels
  S3 = Pushbutton [package="[SMD]"]
  S4 = Pushbutton [package="[SMD]"]
  R2 = Resistor [tolerance=±5% resistance=22k package=THT]
  R3 = Resistor [tolerance=±5% resistance=22k package=THT]
  R4 = Resistor [tolerance=±5% resistance=4.7k package=THT]
  R5 = Resistor [tolerance=±5% resistance=4.7k package=THT]
  R6 = Resistor [tolerance=±5% resistance=47k package=THT]
  R7 = Resistor [tolerance=±5% resistance=47k package=THT]
  XLR2 = XLR3_NCFAH2 [package=xlr3_nc3fah2]
  DIP-Relay1 = DIP-Relay-D31A [part_number=D31A*]
  DIP-Relay2 = DIP-Relay-D31A [part_number=D31A*]
  Q1 = TRANSISTOR_NPN [package=to-92-ammo]
  DIP-Relay3 = DIP-Relay-D31A [part_number=D31A*]
  DIP-Relay4 = DIP-Relay-D31A [part_number=D31A*]
  DIP-Relay5 = DIP-Relay-D31A [part_number=D31A*]
  DIP-Relay6 = DIP-Relay-D31A [part_number=D31A*]
  Q2 = TRANSISTOR_NPN [package=to-92-ammo]

nets:
  N1: R1.Pin_0, Composant1.D2, S3.Pin_1, S3.Pin_2
  GND: R1.Pin_1, Composant1.GND, S2.GND, R2.Pin_1, R3.Pin_1, R4.Pin_0, R5.Pin_0, Q1.C, DIP-Relay4.B2_Switch_Terminal_B, Q2.C
  N2: Composant1.D3, S4.Pin_1, S4.Pin_2, R2.Pin_0
  N3: Composant1.D4, DIP-Relay3.B2_Switch_Terminal_B
  N4: Composant1.D5, DIP-Relay1.B2_Switch_Terminal_B
  N5: Composant1.D6, DIP-Relay2.B2_Switch_Terminal_B
  N6: Composant1.D10, Q1.B
  N7: Composant1.D12/MISO, Q2.B
  5V: Composant1.5V, S1.Pin_3, S1.Pin_4, S2.VCC, S3.Pin_3, S3.Pin_4, S4.Pin_3, S4.Pin_4, DIP-Relay1.Coil2_-, DIP-Relay2.Coil2_-, DIP-Relay3.Coil2_-, DIP-Relay4.Coil2_-, DIP-Relay5.Coil2_-, DIP-Relay6.Coil2_-
  N8: Composant1.A5, S2.SCL
  N9: Composant1.A4, S2.SDA
  N10: Composant1.A2, R4.Pin_1, R6.Pin_0
  N11: Composant1.A0, R5.Pin_1, R7.Pin_0
  N12: Composant1.D13/SCK, S1.Pin_1, S1.Pin_2, R3.Pin_0
  N13: R6.Pin_1, DIP-Relay6.B2_Switch_Terminal_B
  N14: R7.Pin_1, DIP-Relay5.B2_Switch_Terminal_B
  N15: XLR2.1, DIP-Relay3.A2_Switch_Terminal_A, DIP-Relay4.A2_Switch_Terminal_A
  N16: XLR2.2, DIP-Relay1.A2_Switch_Terminal_A, DIP-Relay5.A2_Switch_Terminal_A
  N17: XLR2.3, DIP-Relay2.A2_Switch_Terminal_A, DIP-Relay6.A2_Switch_Terminal_A
  N18: DIP-Relay1.COIL1_+, DIP-Relay2.COIL1_+, Q1.E, DIP-Relay3.COIL1_+
  N19: DIP-Relay4.COIL1_+, DIP-Relay5.COIL1_+, DIP-Relay6.COIL1_+, Q2.E

// code stored in the sketch: Katana.ino
#include <SPI.h>
#include <Wire.h>
#include <Adafruit_GFX.h>
#include <Adafruit_SSD1306.h>

// 'Splash', 128x32px
const unsigned char Splash[] PROGMEM = {
  0xff, 0x3f, 0x80, 0x00, 0x00, 0x00, 0x00, 0x00, 0x00, 0x00, 0x00, 0x00, 0x00, 0x00, 0x00, 0x00, 
  0x3e, 0x1e, 0x00, 0x00, 0x00, 0x00, 0x00, 0x00, 0x00, 0x00, 0x00, 0x00, 0x00, 0x00, 0x00, 0x00, 
  0x3c, 0x18, 0x00, 0x00, 0x00, 0x00, 0x00, 0x00, 0x00, 0x00, 0x00, 0x00, 0x00, 0x00, 0x00, 0x00, 
  0x1c, 0x30, 0x00, 0x00, 0x40, 0x00, 0x00, 0x00, 0x00, 0x00, 0x00, 0x00, 0x00, 0x00, 0x00, 0x00, 
  0x1c, 0x60, 0x00, 0x00, 0x40, 0x00, 0x00, 0x00, 0x00, 0x00, 0x00, 0x00, 0x00, 0x00, 0x00, 0x00, 
  0x1c, 0xc0, 0x00, 0x00, 0xc0, 0x00, 0x00, 0x00, 0x00, 0x00, 0x00, 0x00, 0x00, 0x00, 0x00, 0x00, 
  0x1d, 0x80, 0x00, 0x01, 0xc0, 0x00, 0x00, 0x00, 0x00, 0x00, 0x00, 0x00, 0x00, 0x00, 0x00, 0x70, 
  0x1f, 0xf0, 0x1f, 0xc7, 0xf8, 0x7e, 0x1e, 0x78, 0x3f, 0x80, 0x00, 0x00, 0x00, 0x00, 0x0f, 0xf8, 
  0x1e, 0x78, 0x3d, 0xe1, 0xc0, 0xe7, 0x0f, 0x9c, 0x7b, 0xc0, 0x00, 0x00, 0x00, 0x00, 0xff, 0xf8, 
  0x1c, 0x3c, 0x38, 0xe1, 0xc0, 0xc7, 0x0f, 0x1c, 0x71, 0xc0, 0x00, 0x00, 0x00, 0x1f, 0xff, 0xf8, 
  0x1c, 0x3c, 0x01, 0xe1, 0xc0, 0x07, 0x0f, 0x1e, 0x03, 0xc0, 0x00, 0x20, 0x03, 0xff, 0xff, 0xf8, 
  0x1c, 0x3c, 0x0f, 0xe1, 0xc0, 0x3f, 0x0e, 0x1e, 0x1f, 0xc0, 0x00, 0x20, 0x3f, 0xff, 0xff, 0xc0, 
  0x1c, 0x3c, 0x1c, 0xe1, 0xc0, 0xe7, 0x0e, 0x1c, 0x39, 0xc0, 0x00, 0x37, 0xff, 0xff, 0xfc, 0x00, 
  0x1c, 0x1e, 0x38, 0xe1, 0xc0, 0xc7, 0x0e, 0x1c, 0x71, 0xc0, 0x00, 0x3f, 0xff, 0xff, 0x80, 0x00, 
  0x3c, 0x1e, 0x38, 0xe1, 0xc1, 0xc7, 0x0e, 0x1c, 0x71, 0xc0, 0x03, 0xff, 0xff, 0xf8, 0x00, 0x00, 
  0x3e, 0x1f, 0x39, 0xe1, 0xe4, 0xef, 0x8f, 0x1e, 0x73, 0xc0, 0xff, 0xbf, 0xff, 0x00, 0x00, 0x00, 
  0xff, 0x1f, 0x9e, 0xf0, 0xf8, 0xff, 0xdf, 0xbf, 0x3f, 0xff, 0xfd, 0xbf, 0xf0, 0x00, 0x00, 0x00, 
  0x00, 0x00, 0x00, 0x00, 0x00, 0x00, 0x00, 0x00, 0xff, 0xff, 0x83, 0xfe, 0x00, 0x00, 0x00, 0x00, 
  0x3f, 0xfe, 0x00, 0x00, 0x00, 0x07, 0xff, 0xff, 0xff, 0x1c, 0x70, 0x18, 0x00, 0x00, 0x00, 0x00, 
  0x07, 0xff, 0xff, 0xff, 0xff, 0xff, 0xff, 0xfe, 0x71, 0xe0, 0x00, 0x18, 0x00, 0x00, 0x00, 0x00, 
  0x03, 0x7b, 0xbb, 0xff, 0xff, 0xf3, 0x08, 0x63, 0xc0, 0x0e, 0x00, 0x09, 0xf0, 0x00, 0x00, 0x00, 
  0x00, 0x00, 0x4e, 0x67, 0x31, 0x8c, 0x63, 0x00, 0x00, 0x06, 0x00, 0x03, 0x8c, 0x00, 0x00, 0x00, 
  0x00, 0x00, 0x00, 0x00, 0x00, 0x00, 0x00, 0x00, 0x00, 0x06, 0x00, 0x07, 0x00, 0x00, 0x00, 0x00, 
  0x00, 0x00, 0x00, 0x00, 0x00, 0x00, 0x00, 0x00, 0x00, 0x07, 0xdf, 0x86, 0x01, 0xb9, 0xcf, 0xfc, 
  0x00, 0x00, 0x00, 0x00, 0x00, 0x00, 0x00, 0x00, 0x00, 0x06, 0x6d, 0x06, 0x3f, 0x9b, 0x6c, 0x76, 
  0x00, 0x00, 0x00, 0x00, 0x00, 0x00, 0x00, 0x00, 0x00, 0x06, 0x6d, 0x07, 0x1d, 0x9b, 0xef, 0x66, 
  0x00, 0x00, 0x00, 0x00, 0x00, 0x00, 0x00, 0x00, 0x00, 0x06, 0x66, 0x03, 0x99, 0x9b, 0x03, 0x66, 
  0x00, 0x00, 0x00, 0x00, 0x00, 0x00, 0x00, 0x00, 0x00, 0x05, 0xc6, 0x01, 0xf0, 0xfb, 0xef, 0xfe, 
  0x00, 0x00, 0x00, 0x00, 0x00, 0x00, 0x00, 0x00, 0x00, 0x00, 0x02, 0x00, 0x00, 0x00, 0x00, 0x00, 
  0x00, 0x00, 0x00, 0x00, 0x00, 0x00, 0x00, 0x00, 0x00, 0x00, 0x14, 0x00, 0x00, 0x00, 0x00, 0x00, 
  0x00, 0x00, 0x00, 0x00, 0x00, 0x00, 0x00, 0x00, 0x00, 0x00, 0x18, 0x00, 0x00, 0x00, 0x00, 0x00, 
  0x00, 0x00, 0x00, 0x00, 0x00, 0x00, 0x00, 0x00, 0x00, 0x00, 0x00, 0x00, 0x00, 0x00, 0x00, 0x00
};

// Tableau des fonctions
int maxi = 5;
int minus;
int maximus;
char *fonctions[]={"Testeur 48V", "Generateur 1KHz", "Testeur de cables", "Entree DMX", "Sortie DMX", "Infos"};

//Déclaration des pinout
int Btnup = 2;
int Btndown = 3;
int Btnvalid = 13;

int InLed = LED_BUILTIN;

// Fiche XLR Mâle
int M1 = 4;
int M2 = 5;
int M3 = 6;

// Fiche XLR Femelle
int F1 = 7;
int F2 = 8;
int F3 = 9;

// Routage XLR
int malein = 10;
int femelleout = 11;
int maleanalo = 12;

// Liaisons
char transfert[] = {'-','-','-',0};
char L1[] = {'-','-','-',0};
char L2[] = {'-','-','-',0};
char L3[] = {'-','-','-',0};

// Écran
Adafruit_SSD1306 display = Adafruit_SSD1306(128, 32, &Wire);

// Déclaration des variables
int menu = 0;
int Oldmenu = 9;
int Etatup = 0;
int Oldup = 0;
int Etatdown = 0;
int Olddown = 0;
int Etatvalid = 0;
int Oldvalid = 0;
bool action = false;
int send = 0;


void setup() {

  // init com série
  Serial.begin(115200);
  
  // init écran
  display.begin(SSD1306_SWITCHCAPVCC, 0x3C);
  
  // init boutons
  pinMode(InLed, OUTPUT);
  pinMode(Btnup, INPUT);
  pinMode(Btndown, INPUT);
  
  // init XLR
  pinMode(M1, INPUT);
  pinMode(M2, INPUT);
  pinMode(M3, INPUT);
  pinMode(F1, OUTPUT);
  pinMode(F2, OUTPUT);
  pinMode(F3, OUTPUT);
  
  // init Routage
  pinMode(malein, OUTPUT);
  pinMode(femelleout, OUTPUT);
  pinMode(maleanalo, OUTPUT);

  // Affichage du Splash screen
  display.display();
  display.clearDisplay();
  display.drawBitmap(0, 0, Splash, 128, 32, WHITE);
  display.display();
  delay(2000);
  display.clearDisplay();
  display.display();
  display.setTextColor(SSD1306_WHITE);
  
}  // Void Setup

void loop() {
  // Lecture des entrées
  Etatup = digitalRead(Btnup);
  Etatdown = digitalRead(Btndown);
  Etatvalid = digitalRead(Btnvalid);

  ////////////////
  // Navigation //
  ////////////////

  if (Etatvalid == HIGH && Oldvalid == LOW) {action = !action;}
  Oldvalid = Etatvalid;

  if (action == true){
    switch (menu) {
        case 0:
          T48();
          break;
        case 1:
          G1K();
          break;
        case 2:
          TC();
          break;
        case 3:
          DMXin();
          break;
        case 4:
          DMXout();
          break;
        case 5:
          About();
          break;
    }  // switch menu
    return;
  }

  if (action == false) {
    if (Etatup == HIGH && Oldup == LOW) { menu++; }
    if (Etatdown == HIGH && Olddown == LOW) { menu--; }
    Oldup = Etatup;
    Olddown = Etatdown;

    if (menu == -1) {menu=maxi;}
    if (menu == maxi + 1)  {menu = 0;}
    minus = menu -1;
    maximus = menu +1;
    if (menu == 0) {minus = maxi; maximus = menu + 1;}
    if (menu == maxi) {minus = menu - 1; maximus = 0;} 

    display.clearDisplay();
    display.setCursor(0, 0);
    display.println();
    display.println("--- " + String(fonctions[minus]));
    display.println(">>> " + String(fonctions[menu]));
    display.println("--- " + String(fonctions[maximus]));
    display.display();
  }

}  // Void Loop

void T48() {  // Testeur 48V

  // Établissement routage  
  digitalWrite(malein, LOW);
  digitalWrite(femelleout, LOW);
  digitalWrite(maleanalo, HIGH);

  // Lecture analo
  float inchaud = analogRead(A0);
  float infroid = analogRead(A2);
  float Uchaud = inchaud * 0.056;
  float Ufroid = infroid * 0.056;

  // Affichage données
  display.clearDisplay();
  display.setCursor(0, 0);
  if (Uchaud < 30 || Ufroid < 30) { display.println("Test 48V : Mauvais"); }
  if (Uchaud >= 30 && Uchaud < 35 && Ufroid >= 30 && Ufroid < 35) { display.println("Test 48V : Faible"); }
  if (Uchaud >= 35 && Uchaud < 40 && Ufroid >= 35 && Ufroid < 40) { display.println("Test 48V : Moyen"); }
  if (Uchaud >= 40 && Ufroid >= 40) { display.println("Test 48V : Bon"); }
  display.println("Point chaud : " + String(Uchaud, 0) + "V");
  display.println("Point froid : " + String(Ufroid, 0) + "V");
  display.display();
}  // Void T48

void TC() {  // Testeur de câbles

  // Établissement routage  
  digitalWrite(malein, HIGH);
  digitalWrite(femelleout, HIGH);
  digitalWrite(maleanalo, LOW);

  if (send >= 3) { send = 0; }
  send++;

  digitalWrite(F1, LOW);
  digitalWrite(F2, LOW);
  digitalWrite(F3, LOW);

  switch (send) {
    case 1:
      digitalWrite(F1, HIGH);
      break;
    case 2:
      digitalWrite(F2, HIGH);
      break;
    case 3:
      digitalWrite(F3, HIGH);
      break;
  }

  if (send == 1) { lecture(L1); }
  if (send == 2) { lecture(L2); }
  if (send == 3) { lecture(L3); }
  
  display.clearDisplay();
  display.setCursor(0, 0);
  display.println("Testeur Cable");
  display.println("1 : " + String(L1).substring(0, 3));
  display.println("2 : " + String(L2).substring(0, 3));
  display.println("3 : " + String(L3).substring(0, 3));
  display.display();
}  // Void TC

void G1K() {  // Générateur de fréquence
  display.clearDisplay();
  centrer("Generateur 1KHz",1);
  centrer("Work in progress",3);
  display.display();
}  // Void G1K

void DMXin(){  // Entrée DMX
  display.clearDisplay();
  centrer("Entree DMX",1);
  centrer("Work in progress",3);
  display.display();
} // Void DMXin

void DMXout(){  // Entrée DMX
  display.clearDisplay();
  centrer("Sortie DMX",1);
  centrer("Work in progress",3);
  display.display();
} // Void DMXout

void About(){  // Infos
  display.clearDisplay();
  centrer("Katana",1);
  centrer("By Guesn",2);
  centrer("Version Beta",3);
  centrer("test",4);
  display.display();
}

void lecture(char transfert[5]) {

  // Lecture des entrées pour Testeur de câble
  if (digitalRead(M1)) {transfert[0] = 'X';}
  else {transfert[0] = '-';}
  if (digitalRead(M2)) {transfert[1] = 'X';}
  else {transfert[1] = '-';}
  if (digitalRead(M3)) {transfert[2] = 'X';}
  else {transfert[2] = '-';}
  
  return transfert;
}

void centrer(String message, int ligne){
  display.setCursor((128-(message.length()*6))/2, 8*(ligne-1));
  display.println(String(message));
}
